// Logisim project RiskVCPU.circ as structural Verilog: 3 circuits, main circuit RiskVCPU
module RiskVCPU (
  input  SysClk,
  input  Reset,
  input  PCWEn,
  input  [31:0] Instruction,
  output halt,
  output [31:0] OutTest
);

  wire ASel, BSel, ecall, IF_ID_Flush, IF_ID_WE, MemRead, MemWrite, PC_WE, PCSel, RegWEn, SysClk_t;
  wire [1:0] AddrOffset, ForwardB, FowardA, WBSel;
  wire [2:0] ImmSel, MemByteSel;
  wire [3:0] StoreMask;
  wire [4:0] ALUSel, BrSel, rdi, rs1, rs2;
  wire [31:0] ALUOut, bit_extender_1_out, bit_extender_2_out, IF_ID_Inst, IF_ID_PC, IF_ID_PC_4, ImmGenOut,
       Inst, MemInAligned, MemOut, MemOutAligned, MemWriteData, PC, PCPlus4, RDataA, RDataB, RegWBData;

  Clock clock_1 (.out(SysClk_t));
  // Probe on ALUOut
  // Probe on PC
  // Probe on PCPlus4
  // Probe on Inst
  IMem imem_1 (.PC(PC), .Inst(Inst));
  ProgramCounter programcounter_1 (
    .TargetAddr(ALUOut), .BranchCtl(PCSel), .PCWEn(PC_WE), .Clk(SysClk_t), .Reset(1'b0), .PcOut(PC),
    .PcPlus4(PCPlus4));
  PipelineReg ID_ID_INST (.DataIn(Inst), .WE(IF_ID_WE), .Flush(IF_ID_Flush), .clk(SysClk_t), .DataOut(IF_ID_Inst));
  PipelineReg u_IF_ID_PC (.DataIn(PC), .WE(IF_ID_WE), .Flush(IF_ID_Flush), .clk(SysClk_t), .DataOut(IF_ID_PC));
  PipelineReg u_IF_ID_PC_4 (.DataIn(PCPlus4), .WE(IF_ID_WE), .Flush(IF_ID_Flush), .clk(SysClk_t), .DataOut(IF_ID_PC_4));
  // Probe on ImmGenOut
  // Probe on RDataA
  // Probe on RDataB
  // Probe on RegWBData
  // MainController maincontroller_1: pin names not known; wires that end beside it: IF_ID_Inst, 1'b0, ImmSel, ASel, BSel, ALUSel, BrSel, MemRead, MemWrite, MemByteSel, RegWEn, WBSel, ecall, halt, rdi, rs1, rs2
  ImmGen immgen_1 (.InstIn(IF_ID_Inst), .ImmSelIn(ImmSel), .ImmOut(ImmGenOut));
  RegisterFile registerfile_1 (
    .Data(RegWBData), .RdAddr(rdi), .Rs1Addr(rs1), .Rs2Addr(rs2), .WriteEnable(RegWEn), .Clk(SysClk_t),
    .Rs1Out(RDataA), .Rs2Out(RDataB));
  // Probe on ImmSel
  // Probe on ASel
  // Probe on BSel
  // Probe on ALUSel
  // Probe on BrSel
  // Probe on MemRead
  // Probe on MemWrite
  // Probe on MemByteSel
  // Probe on RegWEn
  // Probe on WBSel
  // Probe on ecall
  // Probe on halt
  // Probe on rdi
  // Probe on rs1
  // Probe on rs2
  HazardControl hazardcontrol_1 (
    .PCSel(PCSel), .PC_WE(PC_WE), .IF_ID_Flush(IF_ID_Flush), .IF_ID_WE(IF_ID_WE), .ForwardA(FowardA),
    .ForwardB(ForwardB));
  // Probe on PCSel
  // Probe on ALUOut
  BranchController branchcontroller_1 (.dataA(RDataA), .dataB(RDataB), .BrSel(BrSel), .TakeBranch(PCSel));
  ALUControl alucontrol_1 (
    .RDataA(RDataA), .PC(IF_ID_PC), .ASel(ASel), .RDataB(RDataB), .ImmVal(ImmGenOut), .BSel(BSel),
    .ALUSel(ALUSel), .Out0(ALUOut));
  // Probe on MemWriteData
  // Probe on RDataB
  // Probe on AddrOffset
  // Probe on MemByteSel
  // Probe on MemOut
  // Probe on MemInAligned
  // Probe on MemOutAligned
  // Probe on AddrOffset
  DMem dmem_1 (
    .AluOut(ALUOut), .MemWrite(MemWrite), .MemRead(MemRead), .StoreMast(StoreMask), .clk(SysClk_t),
    .WriteData(MemWriteData), .AddrOffset(AddrOffset), .MemOut(MemOut));
  StoreAligner storealigner_1 (
    .Data(RDataB), .AddrOffset(AddrOffset), .ByteSel(MemByteSel), .DataOut(MemWriteData), .MaskOut(StoreMask));
  LoadAligner loadaligner_1 (.AddrOffset(AddrOffset), .Data(MemOut), .ByteSel(MemByteSel), .Out0(MemOutAligned));
  // Probe on WBSel
  // Probe on RegWBData
  assign bit_extender_1_out = {{31{MemWrite}}, MemWrite};  // Bit_Extender bit_extender_1
  assign bit_extender_2_out = {{31{halt}}, halt};  // Bit_Extender bit_extender_2
  WriteBackControl writebackcontrol_1 (
    .ALUOut(ALUOut), .MemOut(MemOutAligned), .PCPlus4(IF_ID_PC_4), .WBSel(WBSel), .OutData(RegWBData));
  assign OutTest = MemWriteData & bit_extender_2_out & bit_extender_1_out;  // AND_Gate and_1, 32 bits wide

  // Other names for the same wires on the sheet: ebreak = halt

  // Notes on the sheet:
  //   IF - Instruction Fetch
  //   IF_ID
  //   ID - Instruction Decode
  //   EX - Execute
  //   MEM - Memory
  //   00 = ALU
  //   01 = Mem
  //   11 = PCPlus4
  //   WB - Write Back
endmodule

module PIPELINE_REGS (
);

  wire SysClk;
  wire [31:0] IF_ID_Inst, IF_ID_PC, IF_ID_PC_PLUS_4;

  Register #(.width(32)) u_IF_ID_INST (.D(IF_ID_Inst), .en(1'b1), .clk(SysClk), .Q(IF_ID_Inst));  // open: clr
  Register #(.width(32)) u_IF_ID_PC (.D(IF_ID_PC), .en(1'b1), .clk(SysClk), .Q(IF_ID_PC));  // open: clr
  Register #(.width(32)) u_IF_ID_PC_PLUS_4 (
    .D(IF_ID_PC_PLUS_4), .en(1'b1), .clk(SysClk), .Q(IF_ID_PC_PLUS_4));  // open: clr

  // Other names for the same wires on the sheet: Inst[31:0] = IF_ID_Inst; PC[31:0] = IF_ID_PC;
  //   PCPlus4[31:0] = IF_ID_PC_PLUS_4

  // Notes on the sheet:
  //   IF_ID
endmodule

module PipelineReg (
  input  [31:0] DataIn,
  input  WE,
  input  Flush,
  input  clk,
  output [31:0] DataOut
);

  wire [31:0] multiplexer_1_out;

  // Probe on multiplexer_1_out
  Multiplexer #(.width(32)) multiplexer_1 (.in0(DataIn), .in1({32{1'b0}}), .out(multiplexer_1_out), .sel(Flush));
  Register #(.width(32)) register_1 (.D(multiplexer_1_out), .en(WE), .clk(clk), .Q(DataOut));  // open: clr
  // Probe on DataOut

  // Other names for the same wires on the sheet: data[31:0] = DataIn
endmodule
